# Fritzing sketch Arduino_Nano_ESP32_16x16_LED_matrix (saved by Fritzing 1.0.5)
breadboards: 1

parts:
  S1 = Pushbutton [package="[THT]"]
  Part1 = Logic Level Converter
  R1 = Resistor [tolerance=±5% power=0.25W resistance=330 package=THT]
  C1 = Electrolytic Capacitor [capacitance=1µF voltage=35V package="100 mil [THT, electrolytic]"]
  JACK1 = 2.1mm Barrel Jack with Terminal Block
  U1 = WS2812 RGB LED matrix 8x8  # not connected
  A1 = Arduino Nano ESP32

nets:
  N1: S1.Pin_1, S1.Pin_2, Part1.GND, C1.-, JACK1.POS, A1.Pin_14, A1.Pin_19
  N2: S1.Pin_3, S1.Pin_4, A1.Pin_20
  N3: Part1.LV, A1.Pin_2
  N4: Part1.TX_LV, A1.Pin_24
  N5: Part1.TX_HV, R1.Pin_0
  N6: Part1.HV, C1.+, JACK1.NEG, A1.Pin_12

custom parts:
  WS2812 RGB LED matrix 8x8: WS2812 matrix 8x8
  Arduino Nano ESP32: Arduino® Nano ESP32 tht.
