# Fritzing sketch Arduino_Nano_ESP32_Web-Controlled_2-Axis_Pan-Tilt_Mount (saved by Fritzing 1.0.5)
breadboards: 1

parts:
  SERVO1 = Tower Pro SG90 servo [part_number=101246]
  SERVO2 = Tower Pro SG90 servo [part_number=101246]
  C1 = Electrolytic Capacitor [capacitance=1mF voltage=35V package="100 mil [THT, electrolytic]"]
  JACK1 = 2.1mm Barrel Jack with Terminal Block
  A1 = Arduino Nano ESP32

nets:
  N1: SERVO1.Signal, A1.Pin_13
  +5V: SERVO1.+5V, SERVO2.+5V, C1.+, JACK1.POS
  GND: SERVO1.GND, SERVO2.GND, C1.-, JACK1.NEG, A1.Pin_14, A1.Pin_19
  N2: SERVO2.Signal, A1.Pin_12

custom parts:
  Tower Pro SG90 servo: Original file by John De Cristofaro http://www.adafruit.com/products/1449 Adafruit Feedback Servo (Small) Edited by: e-radionica.com 28/9/2015
  Arduino Nano ESP32: Arduino® Nano ESP32 tht.
