# Fritzing sketch Arduino_Uno_LED_8x8_led_matrix_art (saved by Fritzing 1.0.5)
breadboards: 1

parts:
  Arduino_UNO = Arduino Uno (Rev3)
  Tact_Switch = Pushbutton [package="[THT]"]
  R1 = Resistor [tolerance=±5% power=0.25W resistance=330 package=THT]
  C1 = Electrolytic Capacitor [capacitance=1mF voltage=35V package="100 mil [THT, electrolytic]"]
  U1 = WS2812 RGB LED matrix 8x8
  JACK1 = 2.1mm Barrel Jack with Terminal Block

nets:
  GND: Arduino_UNO.GND, Tact_Switch.Pin_3, Tact_Switch.Pin_4, C1.-, U1.GND, JACK1.POS
  N1: Arduino_UNO.D6_PWM, R1.Pin_0
  N2: C1.+, JACK1.NEG

custom parts:
  WS2812 RGB LED matrix 8x8: WS2812 matrix 8x8
