# Fritzing sketch TestTactSwitch (saved by Fritzing 1.0.5)
breadboards: 1

parts:
  S1 = Pushbutton [package="[THT]"]
  パーツ1 = Arduino Uno (Rev3)

nets:
  N1: S1.Pin_1, S1.Pin_2, パーツ1.D2
  N2: S1.Pin_3, S1.Pin_4, パーツ1.GND
