# Fritzing sketch Arduino_Uno_Chroma_LED (saved by Fritzing 1.0.5)
breadboards: 1

parts:
  Part1 = Arduino Uno (Rev3)
  R1 = Resistor [tolerance=±5% power=0.25W resistance=220 package=THT]
  S3 = Pushbutton [package="[THT]"]
  LED1 = RGB LED (com. cathode, rbg) [color="Red (633nm)" current=0.030A package="5 mm [THT]"]
  R2 = Resistor [tolerance=±5% power=0.25W resistance=220 package=THT]
  R3 = Resistor [tolerance=±5% power=0.25W resistance=220 package=THT]

nets:
  N1: Part1.D9_PWM, R1.Pin_0
  N2: Part1.D10_PWM/SS, R2.Pin_0
  N3: Part1.D11_PWM/MOSI, R3.Pin_0
  N4: Part1.GND, S3.Pin_1, S3.Pin_2, LED1.red_anode
  N5: Part1.D2, S3.Pin_3, S3.Pin_4
  N6: R1.Pin_1, LED1.common_cathode
  N7: LED1.blue_anode, R2.Pin_1
  N8: LED1.green_anode, R3.Pin_1
