# Fritzing sketch Arduino_Uno_Interactive_Servo_Light (saved by Fritzing 1.0.5)
breadboards: 1

parts:
  R1 = Resistor [tolerance=±5% power=0.25W resistance=220 package=THT]
  Part1 = Arduino Uno (Rev3)
  LED1 = RGB LED - (4 legs) [color="Red (633nm)" current=0.030A package="5 mm [THT]"]
  SERVO1 = Tower Pro SG90 servo [part_number=101246]
  R2 = Rotary Potentiometer (Small) [maximum_resistance=10kΩ knob_status=50% power=0.5W package=THT]
  R3 = Resistor [tolerance=±5% power=0.25W resistance=220 package=THT]
  R4 = Resistor [tolerance=±5% power=0.25W resistance=220 package=THT]

nets:
  N1: R1.Pin_0, Part1.D11_PWM/MOSI
  N2: R1.Pin_1, LED1.common_anode
  N3: Part1.A0, R2.wiper
  N4: Part1.D10_PWM/SS, R3.Pin_0
  N5: Part1.D5_PWM, R4.Pin_0
  N6: Part1.D6_PWM, SERVO1.Signal
  5V: Part1.5V, SERVO1.+5V, R2.leg1
  GND: Part1.GND, LED1.red_cathode, SERVO1.GND, R2.leg2
  N7: LED1.green_cathode, R3.Pin_1
  N8: LED1.blue_cathode, R4.Pin_1

custom parts:
  Tower Pro SG90 servo: Original file by John De Cristofaro http://www.adafruit.com/products/1449 Adafruit Feedback Servo (Small) Edited by: e-radionica.com 28/9/2015
