# Fritzing sketch Arduino_Uno_LED_8x8_led_matrix_art (saved by Fritzing 1.0.5)
breadboards: 1

parts:
  Arduino_UNO = Arduino Uno (Rev3)
  8x8_RGB_LED_WS2812B = 8x8 LED Matrix (red)
  Tact_Switch = Pushbutton [package="[THT]"]
  R1 = Resistor [tolerance=±5% power=0.25W resistance=330 package=THT]
  C1 = Electrolytic Capacitor [capacitance=1mF voltage=35V package="100 mil [THT, electrolytic]"]

nets:
  N1: Arduino_UNO.GND, 8x8_RGB_LED_WS2812B.-, 8x8_RGB_LED_WS2812B.C, Tact_Switch.Pin_3, Tact_Switch.Pin_4, C1.-
  N2: Arduino_UNO.D6_PWM, R1.Pin_0
  N3: 8x8_RGB_LED_WS2812B.+, C1.+
  N4: 8x8_RGB_LED_WS2812B.D, R1.Pin_1

custom parts:
  8x8 LED Matrix (red): 8x8 LED Matrix with I2C control (red)
