# Fritzing sketch ESP32-DevKitC_16x16_LED_Matrix (saved by Fritzing 1.0.5)
breadboards: 1

parts:
  U2 = WS2812 RGB LED matrix 8x8
  esp1 = ESP32 DevKitc V4
  S1 = Pushbutton [package="[THT]"]
  Part1 = Logic Level Converter
  R1 = Resistor [tolerance=±5% power=0.25W resistance=330 package=THT]
  C1 = Electrolytic Capacitor [capacitance=1µF voltage=35V package="100 mil [THT, electrolytic]"]
  JACK1 = 2.1mm Barrel Jack with Terminal Block

nets:
  GND: U2.GND, esp1.GND#12, Part1.GND, C1.-, JACK1.POS
  N1: esp1.IO2, S1.Pin_1, S1.Pin_2
  N2: esp1.3V3, Part1.LV
  N3: esp1.IO13, Part1.TX2_LV
  N4: esp1.5V, Part1.HV
  N5: S1.Pin_3, S1.Pin_4
  N6: Part1.TX2_HV, R1.Pin_0
  N7: C1.+, JACK1.NEG

custom parts:
  WS2812 RGB LED matrix 8x8: WS2812 matrix 8x8
  ESP32 DevKitc V4: ESP32-DevKitC board with ESP32-WROOM-32 module. ESP32-DevKitC V4 is a small-sized ESP32-based development board produced by Espressif. Most of the pins on the ESP module are broken out to the pin headers on the board. The pins D0, D1, D2, D3, CMD and CLK are used internally for communication between ESP32 and SPI flash memory. They are grouped on both sides near the USB connector. Avoid using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
