# Fritzing sketch ESP32-DevKitC_Robot_Car (saved by Fritzing 1.0.5)
breadboards: 1

parts:
  M1 = DOIT Esp32 DevKit v1 (30 pins long, 11 pins width) [part_number=ESP32S-PIN30]
  Part1 = Motor Driver 1A Dual TB6612FNG
  S1 = SPST Switch [package=switch-spdt_kit]
  M4 = Getriebemotor
  M5 = Getriebemotor
  VCC1 = 4 x AAA Battery Mount [internal_resistance=0.1Ω]  # not connected

nets:
  3V3: M1.3V3, Part1.VCC
  GND: M1.GND, Part1.GND, S1.S
  N1: M1.D33, Part1.PWMB
  N2: M1.D25, Part1.STBY
  N3: M1.D26, Part1.PWMA
  N4: M1.D27, Part1.AIN2
  N5: M1.D14, Part1.AIN1
  N6: M1.D12, Part1.BIN1
  N7: M1.D13, Part1.BIN2
  N8: M1.VIN, Part1.VM, S1.O
  N9: Part1.B01, M5.pin_1
  N10: Part1.B02, M5.pin_2
  N11: Part1.A02, M4.pin_1
  N12: Part1.A01, M4.pin_2

custom parts:
  DOIT Esp32 DevKit v1 (30 pins long, 11 pins width): The DOIT Esp32 DevKit v1 is one of the development board created by DOIT to evaluate the ESP-WROOM-32 module. It is based on the ESP32 microcontroller that boasts Wifi, Bluetooth, Ethernet and Low Power support all in a single chip. (vanepp) made breadboard work, adjusted pin numbering and labels and reduced size of schematic and cleaned up pcb. This chip is 30pins long (2 x15) and 11 pins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
