# Fritzing sketch ESP32-DevKitC_Web-Controlled_2-Axis_Pan-Tilt_Mount (saved by Fritzing 1.0.5)
breadboards: 1

parts:
  esp1 = ESP32 DevKitc V4
  SERVO1 = Tower Pro SG90 servo [part_number=101246]
  SERVO2 = Tower Pro SG90 servo [part_number=101246]
  C1 = Electrolytic Capacitor [capacitance=1mF voltage=35V package="100 mil [THT, electrolytic]"]
  JACK1 = 2.1mm Barrel Jack with Terminal Block

nets:
  GND: esp1.GND#18, SERVO1.GND, SERVO2.GND, C1.-, JACK1.NEG
  N1: esp1.IO12, SERVO2.Signal
  N2: esp1.IO13, SERVO1.Signal
  +5V: SERVO1.+5V, SERVO2.+5V, C1.+, JACK1.POS

custom parts:
  ESP32 DevKitc V4: ESP32-DevKitC board with ESP32-WROOM-32 module. ESP32-DevKitC V4 is a small-sized ESP32-based development board produced by Espressif. Most of the pins on the ESP module are broken out to the pin headers on the board. The pins D0, D1, D2, D3, CMD and CLK are used internally for communication between ESP32 and SPI flash memory. They are grouped on both sides near the USB connector. Avoid using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
  Tower Pro SG90 servo: Original file by John De Cristofaro http://www.adafruit.com/products/1449 Adafruit Feedback Servo (Small) Edited by: e-radionica.com 28/9/2015
