# Fritzing sketch Seeed_Studio_XIAO_RP2040_16x16_LED_Matrix (saved by Fritzing 1.0.5)
breadboards: 1

parts:
  S1 = Pushbutton [package="[THT]"]
  Part1 = Logic Level Converter
  R1 = Resistor [tolerance=±5% power=0.25W resistance=330 package=THT]
  C1 = Electrolytic Capacitor [capacitance=1µF voltage=35V package="100 mil [THT, electrolytic]"]
  JACK1 = 2.1mm Barrel Jack with Terminal Block
  RP1 = XIAO RP2040 [package="DIP (Dual Inline) [THT]"]
  U1 = WS2812 RGB LED matrix 8x8  # not connected

nets:
  GND: S1.Pin_1, S1.Pin_2, Part1.GND, C1.-, JACK1.POS, RP1.GND
  N1: S1.Pin_3, S1.Pin_4, RP1.D2
  N2: Part1.TX2_LV, RP1.D6
  N3: Part1.LV, RP1.3V3
  N4: Part1.HV, C1.+, JACK1.NEG, RP1.5V
  N5: Part1.TX2_HV, R1.Pin_0

custom parts:
  XIAO RP2040: Seeed Studio XIAO RP2040 is compatible with the Raspberry Pi RP2040 ecosystem as they share the same RP2040 chip. It supports multiple languages including C / MicroPython / CircuitPython. This will be a great tool for you to get started with MicroPython.
  WS2812 RGB LED matrix 8x8: WS2812 matrix 8x8
