# Fritzing sketch Seeed_Studio_XIAO_RP2040_8x8_LED_Matrix (saved by Fritzing 1.0.5)
breadboards: 1

parts:
  U1 = WS2812 RGB LED matrix 8x8  # not connected
  RP1 = XIAO RP2040 [package="DIP (Dual Inline) [THT]"]
  R1 = Resistor [tolerance=±5% power=0.25W resistance=330 package=THT]
  C1 = Electrolytic Capacitor [capacitance=1µF voltage=35V package="100 mil [THT, electrolytic]"]
  S1 = Pushbutton [package="[THT]"]
  JACK1 = 2.1mm Barrel Jack with Terminal Block
  Part1 = Logic Level Converter
  J1 = JST-B3P-VH [part_number=JST-B3P-VH package=THT]

nets:
  N1: RP1.D2, S1.Pin_3, S1.Pin_4
  N2: RP1.D6, Part1.TX2_LV
  N3: RP1.3V3, Part1.LV
  N4: RP1.GND, C1.-, S1.Pin_1, S1.Pin_2, JACK1.NEG, Part1.RX2_HV, Part1.TX2_HV, J1.pin2
  N5: RP1.5V, C1.+, JACK1.POS, J1.pin3
  N6: R1.Pin_0, R1.Pin_1

custom parts:
  WS2812 RGB LED matrix 8x8: WS2812 matrix 8x8
  XIAO RP2040: Seeed Studio XIAO RP2040 is compatible with the Raspberry Pi RP2040 ecosystem as they share the same RP2040 chip. It supports multiple languages including C / MicroPython / CircuitPython. This will be a great tool for you to get started with MicroPython.
