# Fritzing sketch ESP32-DevKitC_8x32_Led_Audio_Spectrum (saved by Fritzing 1.0.5)
breadboards: 1

parts:
  R1 = Resistor [tolerance=±5% power=0.25W resistance=220 package=THT]
  C1 = Electrolytic Capacitor [capacitance=1µF voltage=35V package="100 mil [THT, electrolytic]"]
  Part1 = INMP441
  M1 = DOIT Esp32 DevKit v1 (30 pins long, 11 pins width) [part_number=ESP32S-PIN30]
  U5 = WS2812 RGB LED strip

nets:
  N1: R1.Pin_1, U5.DIN
  GND: C1.-, Part1.GND, M1.GND, U5.GND
  N2: C1.+, U5.VCC
  N3: Part1.WS, M1.D25
  N4: Part1.SCK, M1.D26
  N5: Part1.SD, M1.D34
  VDD: Part1.VDD, M1.3V3

custom parts:
  INMP441: This is a simple breakout board for the INMP441 I2S MEMS microphone.
  DOIT Esp32 DevKit v1 (30 pins long, 11 pins width): The DOIT Esp32 DevKit v1 is one of the development board created by DOIT to evaluate the ESP-WROOM-32 module. It is based on the ESP32 microcontroller that boasts Wifi, Bluetooth, Ethernet and Low Power support all in a single chip. (vanepp) made breadboard work, adjusted pin numbering and labels and reduced size of schematic and cleaned up pcb. This chip is 30pins long (2 x15) and 11 pins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
  WS2812 RGB LED strip: WS2812 strip
